// Logisim project control_logic.circ as structural Verilog: 2 circuits, main circuit control_logic
module control_logic (
  input  [31:0] inst,
  input  BrEq,
  input  BrLt,
  output PCSel,
  output RegWEn,
  output [2:0] ImmSel,
  output BrUn,
  output ASel,
  output BSel,
  output [3:0] ALUSel,
  output MemRW,
  output [1:0] WBSel
);

  wire alu0, alu1, alu2, alu3, alu4, alu5, alu6, alu7, alu8, alu9, alu10, alu11, alu12, alu14, and_1_out,
       and_2_out, and_3_out, and_4_out, and_8_out, and_10_out, and_12_out, and_13_out, and_14_out,
       and_17_out, and_18_out, and_19_out, and_20_out, and_21_out, and_24_out, and_25_out, auipc,
       comparator_1_eq, comparator_2_eq, comparator_3_eq, comparator_4_eq, comparator_5_eq, comparator_6_eq,
       comparator_7_eq, comparator_8_eq, comparator_9_eq, comparator_10_eq, comparator_11_eq,
       comparator_12_eq, comparator_13_eq, comparator_14_eq, comparator_15_eq, comparator_19_eq,
       comparator_20_eq, comparator_21_eq, comparator_22_eq, comparator_23_eq, comparator_24_eq,
       comparator_25_eq, comparator_26_eq, comparator_27_eq, comparator_28_eq, comparator_29_eq,
       comparator_30_eq, comparator_34_eq, comparator_35_eq, comparator_36_eq, comparator_37_eq,
       comparator_38_eq, comparator_39_eq, comparator_43_eq, comparator_44_eq, comparator_45_eq,
       comparator_46_eq, comparator_47_eq, comparator_48_eq, comparator_49_eq, comparator_50_eq,
       demultiplexer_1_out6, demultiplexer_1_out7, Ielse, immI, immU, jal, jalr, lui, lw, or_1_out, R, SB,
       sw, swlt, walu, wpc4;
  wire [1:0] multiplexer_15_out, multiplexer_18_out;
  wire [2:0] multiplexer_7_out, multiplexer_9_out, multiplexer_10_out, multiplexer_11_out, multiplexer_13_out;
  wire [3:0] multiplexer_1_out, multiplexer_2_out, multiplexer_3_out, multiplexer_4_out, multiplexer_5_out,
       multiplexer_6_out, multiplexer_8_out, multiplexer_12_out, multiplexer_14_out, multiplexer_17_out,
       multiplexer_19_out, multiplexer_21_out, multiplexer_22_out;

  Demultiplexer #(.select(3), .enable("false")) demultiplexer_1 (
    .out6(demultiplexer_1_out6), .out7(demultiplexer_1_out7), .in(1'b1), .sel(inst[14:12]));  // open: out0, out1, out2, out3, out4, out5
  Comparator #(.width(3)) comparator_1 (.a(inst[14:12]), .b(3'b001), .eq(comparator_1_eq));  // open: gt, lt
  Comparator #(.width(7)) comparator_2 (.a({7{1'b0}}), .b(inst[31:25]), .eq(comparator_2_eq));  // open: gt, lt
  Comparator #(.width(7)) comparator_3 (.a({7{1'b0}}), .b(inst[31:25]), .eq(comparator_3_eq));  // open: gt, lt
  Multiplexer #(.width(4), .enable("false")) multiplexer_1 (
    .in0(4'b1101), .in1(4'b0000), .out(multiplexer_1_out), .sel(alu0));
  Comparator #(.width(3)) comparator_4 (.a(inst[14:12]), .b(3'b100), .eq(comparator_4_eq));  // open: gt, lt
  Comparator #(.width(7)) comparator_5 (.a({7{1'b0}}), .b(inst[31:25]), .eq(comparator_5_eq));  // open: gt, lt
  Comparator #(.width(3)) comparator_6 (.a(inst[14:12]), .b(3'b100), .eq(comparator_6_eq));  // open: gt, lt
  Comparator #(.width(3)) comparator_7 (.a(inst[14:12]), .b(3'b001), .eq(comparator_7_eq));  // open: gt, lt
  Comparator #(.width(3)) comparator_8 (.a(inst[14:12]), .b(3'b111), .eq(comparator_8_eq));  // open: gt, lt
  Comparator #(.width(7)) comparator_9 (.a(7'b0000001), .b(inst[31:25]), .eq(comparator_9_eq));  // open: gt, lt
  Comparator #(.width(3)) comparator_10 (.a(inst[14:12]), .b(3'b000), .eq(comparator_10_eq));  // open: gt, lt
  Comparator #(.width(7)) comparator_11 (.a(7'b0100000), .b(inst[31:25]), .eq(comparator_11_eq));  // open: gt, lt
  Multiplexer #(.width(4), .enable("false")) multiplexer_2 (
    .in0(multiplexer_1_out), .in1(4'b0001), .out(multiplexer_2_out), .sel(alu1));
  Comparator #(.width(3)) comparator_12 (.a(inst[14:12]), .b(3'b010), .eq(comparator_12_eq));  // open: gt, lt
  or or_1 (or_1_out, demultiplexer_1_out6, demultiplexer_1_out7);
  Comparator #(.width(3)) comparator_13 (.a(inst[14:12]), .b(3'b000), .eq(comparator_13_eq));  // open: gt, lt
  Comparator #(.width(7)) comparator_14 (.a({7{1'b0}}), .b(inst[31:25]), .eq(comparator_14_eq));  // open: gt, lt
  Comparator #(.width(3)) comparator_15 (.a(inst[14:12]), .b(3'b000), .eq(comparator_15_eq));  // open: gt, lt
  and and_1 (and_1_out, comparator_4_eq, R, comparator_5_eq);
  and and_2 (and_2_out, comparator_6_eq, Ielse);
  and and_3 (and_3_out, comparator_1_eq, R, comparator_2_eq);
  and and_4 (and_4_out, comparator_7_eq, Ielse, comparator_3_eq);
  and and_5 (alu9, comparator_8_eq, R, comparator_9_eq);
  and and_6 (alu12, comparator_10_eq, R, comparator_11_eq);
  Multiplexer #(.width(4), .enable("false")) multiplexer_3 (
    .in0(multiplexer_2_out), .in1(4'b0010), .out(multiplexer_3_out), .sel(alu2));
  and and_7 (BrUn, SB, or_1_out);
  or or_2 (immI, lw, jalr, Ielse);
  or or_3 (immU, auipc, lui);
  and and_8 (and_8_out, comparator_15_eq, Ielse);
  or or_4 (alu3, and_1_out, and_2_out);
  or or_5 (alu6, and_3_out, and_4_out);
  Multiplexer #(.width(4), .enable("false")) multiplexer_4 (
    .in0(multiplexer_3_out), .in1(4'b0011), .out(multiplexer_4_out), .sel(alu3));
  Comparator #(.width(7)) comparator_16 (.a(inst[6:0]), .b(7'b0110011), .eq(R));  // open: gt, lt
  Comparator #(.width(7)) comparator_17 (.a(inst[6:0]), .b(7'b0100011), .eq(MemRW));  // open: gt, lt
  Comparator #(.width(7)) comparator_18 (.a(inst[6:0]), .b(7'b0110111), .eq(lui));  // open: gt, lt
  and and_9 (sw, MemRW, comparator_12_eq);
  pcsel1 pcsel1_1 (.jal(jal), .jalr(jalr), .SB(SB), .breq(BrEq), .brlt(BrLt), .func3(inst[14:12]), .pcsel(PCSel));
  or or_6 (ASel, jal, SB, auipc);
  and and_10 (and_10_out, comparator_13_eq, R, comparator_14_eq);
  Multiplexer #(.width(4), .enable("false")) multiplexer_5 (
    .in0(multiplexer_4_out), .in1(4'b0100), .out(multiplexer_5_out), .sel(alu4));
  Multiplexer #(.width(4), .enable("false")) multiplexer_6 (
    .in0(multiplexer_5_out), .in1(4'b0101), .out(multiplexer_6_out), .sel(alu5));
  Comparator #(.width(3)) comparator_19 (.a(inst[14:12]), .b(3'b111), .eq(comparator_19_eq));  // open: gt, lt
  Multiplexer #(.width(3), .enable("false")) multiplexer_7 (
    .in0(3'b110), .in1(3'b000), .out(multiplexer_7_out), .sel(immI));
  or or_7 (alu0, and_10_out, lw, MemRW, SB, auipc, jal, jalr, and_8_out);
  Comparator #(.width(3)) comparator_20 (.a(inst[14:12]), .b(3'b101), .eq(comparator_20_eq));  // open: gt, lt
  Comparator #(.width(7)) comparator_21 (.a({7{1'b0}}), .b(inst[31:25]), .eq(comparator_21_eq));  // open: gt, lt
  Comparator #(.width(3)) comparator_22 (.a(inst[14:12]), .b(3'b101), .eq(comparator_22_eq));  // open: gt, lt
  Comparator #(.width(7)) comparator_23 (.a({7{1'b0}}), .b(inst[31:25]), .eq(comparator_23_eq));  // open: gt, lt
  Comparator #(.width(3)) comparator_24 (.a(inst[14:12]), .b(3'b010), .eq(comparator_24_eq));  // open: gt, lt
  Comparator #(.width(7)) comparator_25 (.a({7{1'b0}}), .b(inst[31:25]), .eq(comparator_25_eq));  // open: gt, lt
  Comparator #(.width(3)) comparator_26 (.a(inst[14:12]), .b(3'b010), .eq(comparator_26_eq));  // open: gt, lt
  Comparator #(.width(3)) comparator_27 (.a(inst[14:12]), .b(3'b000), .eq(comparator_27_eq));  // open: gt, lt
  Comparator #(.width(7)) comparator_28 (.a(7'b0000001), .b(inst[31:25]), .eq(comparator_28_eq));  // open: gt, lt
  Comparator #(.width(3)) comparator_29 (.a(inst[14:12]), .b(3'b001), .eq(comparator_29_eq));  // open: gt, lt
  Comparator #(.width(7)) comparator_30 (.a(7'b0000001), .b(inst[31:25]), .eq(comparator_30_eq));  // open: gt, lt
  Multiplexer #(.width(4), .enable("false")) multiplexer_8 (
    .in0(multiplexer_6_out), .in1(4'b0110), .out(multiplexer_8_out), .sel(alu6));
  or or_8 (walu, R, auipc, Ielse, lui);
  or or_9 (wpc4, jalr, jal);
  and and_11 (swlt, MemRW, comparator_19_eq);
  Multiplexer #(.width(3), .enable("false")) multiplexer_9 (
    .in0(multiplexer_7_out), .in1(3'b001), .out(multiplexer_9_out), .sel(sw));
  Multiplexer #(.width(3), .enable("false")) multiplexer_10 (
    .in0(multiplexer_9_out), .in1(3'b010), .out(multiplexer_10_out), .sel(SB));
  and and_12 (and_12_out, comparator_22_eq, Ielse, comparator_23_eq);
  and and_13 (and_13_out, comparator_24_eq, R, comparator_25_eq);
  and and_14 (and_14_out, comparator_26_eq, Ielse);
  and and_15 (alu10, comparator_27_eq, R, comparator_28_eq);
  and and_16 (alu14, comparator_29_eq, R, comparator_30_eq);
  Comparator #(.width(7)) comparator_31 (.a(inst[6:0]), .b(7'b0000011), .eq(lw));  // open: gt, lt
  Comparator #(.width(7)) comparator_32 (.a(inst[6:0]), .b(7'b1100011), .eq(SB));  // open: gt, lt
  Comparator #(.width(7)) comparator_33 (.a(inst[6:0]), .b(7'b1101111), .eq(jal));  // open: gt, lt
  Multiplexer #(.width(3), .enable("false")) multiplexer_11 (
    .in0(multiplexer_10_out), .in1(3'b011), .out(multiplexer_11_out), .sel(immU));
  not not_1 (BSel, R);
  Comparator #(.width(7)) comparator_34 (.a({7{1'b0}}), .b(inst[31:25]), .eq(comparator_34_eq));  // open: gt, lt
  Comparator #(.width(3)) comparator_35 (.a(inst[14:12]), .b(3'b110), .eq(comparator_35_eq));  // open: gt, lt
  Comparator #(.width(7)) comparator_36 (.a({7{1'b0}}), .b(inst[31:25]), .eq(comparator_36_eq));  // open: gt, lt
  and and_17 (and_17_out, comparator_20_eq, R, comparator_21_eq);
  or or_10 (alu7, and_13_out, and_14_out);
  Multiplexer #(.width(4), .enable("false")) multiplexer_12 (
    .in0(multiplexer_8_out), .in1(4'b0111), .out(multiplexer_12_out), .sel(alu7));
  Multiplexer #(.width(3), .enable("false")) multiplexer_13 (
    .in0(multiplexer_11_out), .in1(3'b100), .out(multiplexer_13_out), .sel(jal));
  Comparator #(.width(3)) comparator_37 (.a(inst[14:12]), .b(3'b111), .eq(comparator_37_eq));  // open: gt, lt
  Comparator #(.width(3)) comparator_38 (.a(inst[14:12]), .b(3'b111), .eq(comparator_38_eq));  // open: gt, lt
  Comparator #(.width(3)) comparator_39 (.a(inst[14:12]), .b(3'b110), .eq(comparator_39_eq));  // open: gt, lt
  or or_11 (alu4, and_17_out, and_12_out);
  Multiplexer #(.width(4), .enable("false")) multiplexer_14 (
    .in0(multiplexer_12_out), .in1(4'b1000), .out(multiplexer_14_out), .sel(alu8));
  Multiplexer #(.width(2), .enable("false")) multiplexer_15 (
    .in0(2'b11), .in1(2'b00), .out(multiplexer_15_out), .sel(lw));
  Multiplexer #(.width(3), .enable("false")) multiplexer_16 (
    .in0(multiplexer_13_out), .in1(3'b101), .out(ImmSel), .sel(swlt));
  and and_18 (and_18_out, comparator_37_eq, R, comparator_34_eq);
  and and_19 (and_19_out, comparator_38_eq, Ielse);
  and and_20 (and_20_out, comparator_35_eq, R, comparator_36_eq);
  and and_21 (and_21_out, comparator_39_eq, Ielse);
  Multiplexer #(.width(4), .enable("false")) multiplexer_17 (
    .in0(multiplexer_14_out), .in1(4'b1001), .out(multiplexer_17_out), .sel(alu9));
  Multiplexer #(.width(2), .enable("false")) multiplexer_18 (
    .in0(multiplexer_15_out), .in1(2'b01), .out(multiplexer_18_out), .sel(walu));
  Comparator #(.width(7)) comparator_40 (.a(inst[6:0]), .b(7'b0010011), .eq(Ielse));  // open: gt, lt
  Comparator #(.width(7)) comparator_41 (.a(inst[6:0]), .b(7'b0010111), .eq(auipc));  // open: gt, lt
  Comparator #(.width(7)) comparator_42 (.a(inst[6:0]), .b(7'b1100111), .eq(jalr));  // open: gt, lt
  or or_12 (RegWEn, R, Ielse, lw, auipc, lui, jal, jalr);
  or or_13 (alu1, and_18_out, and_19_out);
  or or_14 (alu2, and_20_out, and_21_out);
  Comparator #(.width(3)) comparator_43 (.a(inst[14:12]), .b(3'b101), .eq(comparator_43_eq));  // open: gt, lt
  Comparator #(.width(7)) comparator_44 (.a(7'b0100000), .b(inst[31:25]), .eq(comparator_44_eq));  // open: gt, lt
  Comparator #(.width(3)) comparator_45 (.a(inst[14:12]), .b(3'b101), .eq(comparator_45_eq));  // open: gt, lt
  Comparator #(.width(7)) comparator_46 (.a(7'b0100000), .b(inst[31:25]), .eq(comparator_46_eq));  // open: gt, lt
  Comparator #(.width(3)) comparator_47 (.a(inst[14:12]), .b(3'b101), .eq(comparator_47_eq));  // open: gt, lt
  Comparator #(.width(7)) comparator_48 (.a(7'b0000001), .b(inst[31:25]), .eq(comparator_48_eq));  // open: gt, lt
  Comparator #(.width(3)) comparator_49 (.a(inst[14:12]), .b(3'b011), .eq(comparator_49_eq));  // open: gt, lt
  Comparator #(.width(7)) comparator_50 (.a(7'b0000001), .b(inst[31:25]), .eq(comparator_50_eq));  // open: gt, lt
  Multiplexer #(.width(4), .enable("false")) multiplexer_19 (
    .in0(multiplexer_17_out), .in1(4'b1010), .out(multiplexer_19_out), .sel(alu10));
  Multiplexer #(.width(2), .enable("false")) multiplexer_20 (
    .in0(multiplexer_18_out), .in1(2'b10), .out(WBSel), .sel(wpc4));
  and and_22 (alu8, comparator_47_eq, R, comparator_48_eq);
  and and_23 (alu11, comparator_49_eq, R, comparator_50_eq);
  Multiplexer #(.width(4), .enable("false")) multiplexer_21 (
    .in0(multiplexer_19_out), .in1(4'b1011), .out(multiplexer_21_out), .sel(alu11));
  and and_24 (and_24_out, comparator_43_eq, R, comparator_44_eq);
  and and_25 (and_25_out, comparator_45_eq, Ielse, comparator_46_eq);
  Multiplexer #(.width(4), .enable("false")) multiplexer_22 (
    .in0(multiplexer_21_out), .in1(4'b1100), .out(multiplexer_22_out), .sel(alu12));
  or or_15 (alu5, and_24_out, and_25_out);
  Multiplexer #(.width(4), .enable("false")) multiplexer_23 (
    .in0(multiplexer_22_out), .in1(4'b1110), .out(ALUSel), .sel(alu14));

  // Other names for the same wires on the sheet: opcode[6:0] = inst[6:0]; func3[2:0] = inst[14:12];
  //   func7[6:0] = inst[31:25]; S = MemRW

  // Notes on the sheet:
  //   INPUTS to your circuit
  //   DON'T CHANGE THE LOCATIONS OF THE INPUTS AND OUTPUTS!
  //   OUTPUT from your circuit
endmodule

module pcsel1 (
  input  jal,
  input  jalr,
  input  SB,
  input  breq,
  input  brlt,
  input  [2:0] func3,
  output pcsel
);

  wire and_1_out, and_2_out, and_3_out, and_4_out, and_5_out, and_6_out, and_7_out, beq, bge, bgeu, blt,
       bltu, bne, not_1_out, not_2_out, not_3_out, tojump;

  Demultiplexer #(.select(3), .enable("false")) demultiplexer_1 (
    .out0(beq), .out1(bne), .out4(blt), .out5(bge), .out6(bltu), .out7(bgeu), .in(1'b1), .sel(func3));  // open: out2, out3
  and and_1 (and_1_out, SB, tojump);
  or or_1 (pcsel, jalr, jal, and_1_out);
  not not_1 (not_1_out, breq);
  not not_2 (not_2_out, brlt);
  not not_3 (not_3_out, brlt);
  and and_2 (and_2_out, breq, beq);
  and and_3 (and_3_out, bne, not_1_out);
  and and_4 (and_4_out, blt, brlt);
  and and_5 (and_5_out, bge, not_2_out);
  and and_6 (and_6_out, bltu, brlt);
  and and_7 (and_7_out, bgeu, not_3_out);
  or or_2 (tojump, and_2_out, and_3_out, and_4_out, and_5_out, and_6_out, and_7_out);
endmodule
