// Logisim project cpu.circ as structural Verilog: 1 circuit, main circuit main
module main (
  input  [31:0] INSTRUCTION,
  input  CLOCK,
  output [31:0] PROGRAM_COUNTER,
  output [31:0] ra,
  output [31:0] sp,
  output [31:0] t0,
  output [31:0] t1,
  output [31:0] t2,
  output [31:0] s0,
  output [31:0] s1,
  output [31:0] a0
);

  wire asel, branch_comp_1_breq, branch_comp_1_brlt, bsel, control_logic_1_brun, control_logic_1_memrw,
       control_logic_1_regwen, pcsel;
  wire [1:0] control_logic_1_wbsel;
  wire [2:0] immsel;
  wire [3:0] control_logic_1_alusel;
  wire [31:0] ari0, dat1, dat2, delayinst, delaypc1, DMEM_read_data, imm0, multiplexer_1_out,
       multiplexer_2_out, multiplexer_3_out, multiplexer_4_out, pc4, register_4_q, wbdat;

  control_logic control_logic_1 (
    .BSel(bsel), .RegWEn(control_logic_1_regwen), .ASel(asel), .ImmSel(immsel), .BrUn(control_logic_1_brun),
    .PCSel(pcsel), .BrLt(branch_comp_1_brlt), .BrEq(branch_comp_1_breq), .inst(delayinst),
    .ALUSel(control_logic_1_alusel), .MemRW(control_logic_1_memrw), .WBSel(control_logic_1_wbsel));
  Adder #(.width(32)) adder_1 (.a(PROGRAM_COUNTER), .b(32'h4), .out(pc4));  // open: cin, cout
  Multiplexer #(.width(32), .enable("false")) multiplexer_1 (
    .in0(pc4), .in1(ari0), .out(multiplexer_1_out), .sel(pcsel));
  Register #(.width(32)) PC (.D(multiplexer_1_out), .clk(CLOCK), .Q(PROGRAM_COUNTER));  // open: en, clr
  imm_gen imm_gen_1 (.ImmSel(immsel), .inst(delayinst), .imm(imm0));
  Multiplexer #(.width(32), .enable("false")) multiplexer_2 (
    .in0(INSTRUCTION), .in1(32'h13), .out(multiplexer_2_out), .sel(pcsel));
  Register #(.width(32)) register_1 (.D(multiplexer_2_out), .clk(CLOCK), .Q(delayinst));  // open: en, clr
  regfile_main RegFile (
    .rs2(delayinst[24:20]), .rd(delayinst[11:7]), .Read_Data_1(dat1), .Read_Data_2(dat2), .ra(ra), .sp(sp),
    .t0(t0), .t1(t1), .t2(t2), .s0(s0), .s1(s1), .a0(a0), .rs1(delayinst[19:15]), .Write_Data(wbdat),
    .RegWEn(control_logic_1_regwen), .clk(CLOCK));
  branch_comp branch_comp_1 (
    .BrEq(branch_comp_1_breq), .BrUn(control_logic_1_brun), .rs1(dat1), .BrLt(branch_comp_1_brlt), .rs2(dat2));
  Multiplexer #(.width(32), .enable("false")) multiplexer_3 (
    .in0(dat1), .in1(delaypc1), .out(multiplexer_3_out), .sel(asel));
  Multiplexer #(.width(32), .enable("false")) multiplexer_4 (
    .in0(dat2), .in1(imm0), .out(multiplexer_4_out), .sel(bsel));
  alu Arithmetic_Logic_Unit (
    .ALUSel(control_logic_1_alusel), .Result(ari0), .A(multiplexer_3_out), .B(multiplexer_4_out));
  Register #(.width(32)) register_2 (.D(PROGRAM_COUNTER), .clk(CLOCK), .Q(delaypc1));  // open: en, clr
  Register #(.width(32)) register_3 (.clk(CLOCK));  // open: D, en, Q, clr
  mem_main DMEM (
    .Address(ari0), .Write_Data(dat2), .Write_En(control_logic_1_memrw), .Read_Data(DMEM_read_data),
    .clk(CLOCK));
  Register #(.width(32)) register_4 (.D(pc4), .clk(CLOCK), .Q(register_4_q));  // open: en, clr
  Multiplexer #(.select(2), .width(32), .enable("false")) multiplexer_5 (
    .in0(DMEM_read_data), .in1(ari0), .in2(register_4_q), .out(wbdat), .sel(control_logic_1_wbsel));  // open: in3

  // Other names for the same wires on the sheet: clk = CLOCK; rd0[4:0] = delayinst[11:7];
  //   rs10[4:0] = delayinst[19:15]; rs20[4:0] = delayinst[24:20]

  // Notes on the sheet:
  //   Output
  //   IMEM (do **NOT** move this)
  //   Inputs
  //   Inputs/Outputs for testing. Do **NOT** move these.
endmodule
