// Logisim project imm_gen.circ as structural Verilog: 1 circuit, main circuit imm_gen
module imm_gen (
  input  [31:0] inst,
  input  [2:0] ImmSel,
  output [31:0] imm
);

  wire comparator_1_eq;
  wire [31:0] Itype, SBtype, Stype, UJtype;

  Comparator #(.width(3)) comparator_1 (.a(ImmSel), .b(3'b101), .eq(comparator_1_eq));  // open: gt, lt
  Multiplexer #(.width(32), .enable("false")) multiplexer_1 (
    .in1({32{1'b0}}), .out(imm), .sel(comparator_1_eq));  // open: in0
  assign Itype = {{20{inst[31]}}, inst[31:20]};  // Bit_Extender bit_extender_1
  assign Stype = {{20{inst[31]}}, {inst[31:25], inst[11:7]}};  // Bit_Extender bit_extender_2
  assign SBtype = {{19{inst[31]}}, {inst[31], inst[7], inst[30:25], inst[11:8], 1'b0}};  // Bit_Extender bit_extender_3
  Multiplexer #(.select(3), .width(32), .enable("false")) multiplexer_2 (
    .in0(Itype), .in1(Stype), .in2(SBtype), .in3({inst[31:12], {12{1'b0}}}), .in4(UJtype), .out(imm),
    .sel(ImmSel));  // open: in5, in6, in7
  assign UJtype = {{11{inst[31]}}, {inst[31], inst[19:12], inst[20], inst[30:21], 1'b0}};  // Bit_Extender bit_extender_4

  // Other names for the same wires on the sheet: Utype[31:12] = inst[31:12]

  // Notes on the sheet:
  //   INPUTS to your circuit
  //   set imm to 0, for inst that need rs1
  //   DON'T CHANGE THE LOCATIONS OF THE INPUTS AND OUTPUTS!
  //   OUTPUT from your circuit
endmodule
